// Logisim project EP01.circ as structural Verilog: 5 circuits, main circuit main
module main (
  input  A0,
  input  Ci,
  input  A1,
  input  A2,
  input  A3,
  input  B0,
  input  B1,
  input  B2,
  input  B3,
  output S0,
  output S1,
  output S2,
  output S3,
  output Co
);

  wire decodificador_1_a, decodificador_1_b, decodificador_1_c, decodificador_1_d, decodificador_1_e,
       decodificador_1_f, decodificador_1_g, decodificador_2_a, decodificador_2_b, decodificador_2_c,
       decodificador_2_d, decodificador_2_e, decodificador_2_f, decodificador_2_g, decodificador_3_a,
       decodificador_3_b, decodificador_3_c, decodificador_3_d, decodificador_3_e, decodificador_3_f,
       decodificador_3_g;

  soma_4bit soma_4bit_1 (
    .B3(B3), .A3(A3), .B2(B2), .A2(A2), .B1(B1), .A1(A1), .B0(B0), .A0(A0), .C0(Co), .S3(S3), .S2(S2),
    .S1(S1), .S0(S0), .Ci0(Ci));
  decodificador decodificador_1 (
    .S0(B3), .S1(B2), .S2(B1), .A(decodificador_1_a), .S3(B0), .B(decodificador_1_b), .C(decodificador_1_c),
    .D(decodificador_1_d), .E(decodificador_1_e), .F(decodificador_1_f), .G(decodificador_1_g));
  decodificador decodificador_2 (
    .S0(A3), .S1(A2), .S2(A1), .A(decodificador_2_a), .S3(A0), .B(decodificador_2_b), .C(decodificador_2_c),
    .D(decodificador_2_d), .E(decodificador_2_e), .F(decodificador_2_f), .G(decodificador_2_g));
  _7_Segment_Display u_7_segment_display_1 (
    .g(decodificador_2_g), .f(decodificador_2_f), .a(decodificador_2_a), .b(decodificador_2_b),
    .e(decodificador_2_e), .d(decodificador_2_d), .c(decodificador_2_c));  // open: dp
  _7_Segment_Display u_7_segment_display_2 (
    .g(decodificador_1_g), .f(decodificador_1_f), .a(decodificador_1_a), .b(decodificador_1_b),
    .e(decodificador_1_e), .d(decodificador_1_d), .c(decodificador_1_c));  // open: dp
  decodificador decodificador_3 (
    .S0(S3), .S1(S2), .S2(S1), .A(decodificador_3_a), .S3(S0), .B(decodificador_3_b), .C(decodificador_3_c),
    .D(decodificador_3_d), .E(decodificador_3_e), .F(decodificador_3_f), .G(decodificador_3_g));
  _7_Segment_Display u_7_segment_display_3 (
    .g(decodificador_3_g), .f(decodificador_3_f), .a(decodificador_3_a), .b(decodificador_3_b),
    .e(decodificador_3_e), .d(decodificador_3_d), .c(decodificador_3_c));  // open: dp

  // Notes on the sheet:
  //   Overflow
endmodule

// Meia soma
module meia_soma (
  input  X,
  input  Y,
  output S1,
  output out_4
);

  and and_1 (out_4, Y, X);
  xor xor_1 (S1, X, Y);
endmodule

// Soma completa
module soma_completa (
  input  A0,
  input  B0,
  input  Ci0,
  output S0,
  output Co0
);

  wire meia_soma_1_out_4, meia_soma_1_s1, meia_soma_2_out_4;

  meia_soma meia_soma_1 (.X(A0), .Y(B0), .S1(meia_soma_1_s1), .out_4(meia_soma_1_out_4));
  meia_soma meia_soma_2 (.X(meia_soma_1_s1), .Y(Ci0), .S1(S0), .out_4(meia_soma_2_out_4));
  or or_1 (Co0, meia_soma_1_out_4, meia_soma_2_out_4);
endmodule

// Somador 4 bits
module soma_4bit (
  input  A3,
  input  A2,
  input  A1,
  input  A0,
  input  B3,
  input  B2,
  input  B1,
  input  B0,
  input  Ci0,
  output S3,
  output S2,
  output S1,
  output S0,
  output C0
);

  wire soma_completa_2_co0, soma_completa_3_co0, soma_completa_4_co0;

  soma_completa soma_completa_1 (.A0(A3), .B0(B3), .Ci0(soma_completa_2_co0), .S0(S3), .Co0(C0));
  soma_completa soma_completa_2 (.A0(A2), .B0(B2), .Ci0(soma_completa_3_co0), .S0(S2), .Co0(soma_completa_2_co0));
  soma_completa soma_completa_3 (.A0(A1), .B0(B1), .Ci0(soma_completa_4_co0), .S0(S1), .Co0(soma_completa_3_co0));
  soma_completa soma_completa_4 (.A0(A0), .B0(B0), .Ci0(Ci0), .S0(S0), .Co0(soma_completa_4_co0));
endmodule

// Decodificador
module decodificador (
  input  S0,
  input  S1,
  input  S2,
  input  S3,
  output A,
  output B,
  output C,
  output D,
  output E,
  output F,
  output G
);

  wire and_1_out, and_2_out, and_3_out, and_4_out, and_5_out, and_6_out, and_7_out, and_8_out, and_9_out,
       and_10_out, and_11_out, and_12_out, and_13_out, and_14_out, and_15_out, and_16_out, and_17_out,
       and_18_out, and_19_out, and_20_out, and_21_out, and_22_out, and_23_out, and_24_out, and_25_out,
       and_26_out, and_27_out, and_28_out, and_29_out, and_30_out, and_31_out, and_32_out, and_33_out,
       and_34_out, and_35_out, not_1_out, not_2_out, not_3_out, not_4_out, not_5_out, not_6_out, not_7_out,
       not_8_out, not_9_out, not_10_out, not_11_out, not_12_out, not_13_out, not_14_out, not_15_out,
       not_16_out, not_17_out, not_18_out, not_19_out, not_20_out, not_21_out, not_22_out, not_23_out,
       not_24_out, not_25_out, not_26_out, not_27_out, not_28_out, not_29_out, not_30_out, not_31_out,
       not_32_out, not_33_out, not_34_out, not_35_out, not_36_out, not_37_out, not_38_out, not_39_out,
       not_40_out, not_41_out, not_42_out, not_43_out;

  not not_1 (not_1_out, S1);
  and and_1 (and_1_out, not_1_out, not_2_out);
  not not_2 (not_2_out, S3);
  not not_3 (not_3_out, S0);
  and and_2 (and_2_out, not_3_out, S2);
  not not_4 (not_4_out, S0);
  and and_3 (and_3_out, not_4_out, S1, S3);
  and and_4 (and_4_out, S1, S2);
  not not_5 (not_5_out, S1);
  and and_5 (and_5_out, S0, not_5_out, not_6_out);
  not not_6 (not_6_out, S2);
  and and_6 (and_6_out, S0, not_7_out);
  not not_7 (not_7_out, S3);
  not not_8 (not_8_out, S0);
  and and_7 (and_7_out, not_8_out, not_9_out);
  not not_9 (not_9_out, S1);
  not not_10 (not_10_out, S0);
  and and_8 (and_8_out, not_10_out, not_11_out, not_12_out);
  not not_11 (not_11_out, S2);
  not not_12 (not_12_out, S3);
  not not_13 (not_13_out, S1);
  and and_9 (and_9_out, not_13_out, not_14_out);
  not not_14 (not_14_out, S3);
  not not_15 (not_15_out, S0);
  and and_10 (and_10_out, not_15_out, S2, S3);
  not not_16 (not_16_out, S2);
  and and_11 (and_11_out, S0, not_16_out, S3);
  not not_17 (not_17_out, S0);
  and and_12 (and_12_out, not_17_out, not_18_out);
  not not_18 (not_18_out, S2);
  not not_19 (not_19_out, S0);
  and and_13 (and_13_out, not_19_out, S3);
  not not_20 (not_20_out, S2);
  and and_14 (and_14_out, not_20_out, S3);
  not not_21 (not_21_out, S0);
  and and_15 (and_15_out, not_21_out, S1);
  and and_16 (and_16_out, S0, not_22_out);
  not not_22 (not_22_out, S1);
  not not_23 (not_23_out, S0);
  and and_17 (and_17_out, not_23_out, not_24_out, not_25_out);
  not not_24 (not_24_out, S1);
  not not_25 (not_25_out, S3);
  not not_26 (not_26_out, S1);
  and and_18 (and_18_out, not_26_out, S2, S3);
  and and_19 (and_19_out, S1, not_27_out, S3);
  not not_27 (not_27_out, S2);
  and and_20 (and_20_out, S1, S2, not_28_out);
  not not_28 (not_28_out, S3);
  and and_21 (and_21_out, S0, not_29_out);
  not not_29 (not_29_out, S2);
  not not_30 (not_30_out, S1);
  and and_22 (and_22_out, not_30_out, not_31_out);
  not not_31 (not_31_out, S3);
  and and_23 (and_23_out, S2, not_32_out);
  not not_32 (not_32_out, S3);
  and and_24 (and_24_out, S0, S2);
  and and_25 (and_25_out, S0, S1);
  not not_33 (not_33_out, S2);
  and and_26 (and_26_out, not_33_out, not_34_out);
  not not_34 (not_34_out, S3);
  not not_35 (not_35_out, S0);
  and and_27 (and_27_out, not_35_out, S1, not_36_out);
  not not_36 (not_36_out, S2);
  and and_28 (and_28_out, S1, not_37_out);
  not not_37 (not_37_out, S3);
  and and_29 (and_29_out, S0, not_38_out);
  not not_38 (not_38_out, S1);
  and and_30 (and_30_out, S0, S2);
  not not_39 (not_39_out, S1);
  and and_31 (and_31_out, not_39_out, S2);
  and and_32 (and_32_out, S2, not_40_out);
  not not_40 (not_40_out, S3);
  not not_41 (not_41_out, S0);
  and and_33 (and_33_out, not_41_out, S1, not_42_out);
  not not_42 (not_42_out, S2);
  and and_34 (and_34_out, S0, not_43_out);
  not not_43 (not_43_out, S1);
  and and_35 (and_35_out, S0, S3);
  or or_1 (B, and_7_out, and_8_out, and_9_out, and_10_out, and_11_out);
  or or_2 (C, and_12_out, and_13_out, and_14_out, and_15_out, and_16_out);
  or or_3 (D, and_17_out, and_18_out, and_19_out, and_20_out, and_21_out);
  or or_4 (E, and_22_out, and_23_out, and_24_out, and_25_out);
  or or_5 (F, and_26_out, and_27_out, and_28_out, and_29_out, and_30_out);
  or or_6 (G, and_31_out, and_32_out, and_33_out, and_34_out, and_35_out);
  or or_7 (A, and_1_out, and_2_out, and_3_out, and_4_out, and_5_out, and_6_out);
endmodule
